# Fritzing sketch receiver (saved by Fritzing 0.7.0b)
breadboards: 1

parts:
  LED1 = Red LED - 5mm
  1k = 220 Ω Resistor [package=THT]
  Arduino2 = Arduino
  DS18B20 = Mystery Part - 3 pins [package=THT]  # not connected
  5k = 220 Ω Resistor [package=THT]

nets (from the breadboard view):
  N1: LED1.cathode, Arduino2.GND
  N2: LED1.anode, 1k.Pin_0
  N3: 1k.Pin_1, Arduino2.D9
  N4: Arduino2.D8, 5k.Pin_0
  N5: Arduino2.+5V, 5k.Pin_1

custom parts:
  Mystery Part - 3 pins: A dummy, proxy, ersatz, stand-in part for whatever you want. With 3 pins on a 100 mil inline pin header footprint.
